# Fritzing sketch Alarm_Clock_Simon_Schematic_Stack (saved by Fritzing 0.7.12b)
breadboards: 3

parts:
  J1 = Piezo Speaker
  IC3 = IC, DIP package, 24 pins [chip_label=MAX2719]
  J7 = female pin header, 6 pins [form="♀ (female)"]
  J8 = female pin header, 6 pins [form="♀ (female)"]
  R7 = Resistor [tolerance=±5% resistance=220 package=THT]
  C6 = Ceramic Capacitor [capacitance=100nF package="100 mil [THT, multilayer]"]
  U5 = atmega328 [package=dip]
  C10 = Electrolytic Capacitor [capacitance=10µF package="100 mil [THT, electrolytic]"]
  XTAL3 = Crystal [frequency="16 Mhz" package=THT]
  C11 = Ceramic Capacitor [capacitance=100nF package="100 mil [THT, multilayer]"]
  C12 = Electrolytic Capacitor [capacitance=10µF package="100 mil [THT, electrolytic]"]
  C13 = Ceramic Capacitor [capacitance=100nF package="100 mil [THT, multilayer]"]
  U6 = Voltage Regulator - 5V [package="TO220 [THT]"]
  IC4 = DS1307 [package=THT]
  Xtal = female pin header, 1 pin [form="♀ (female)"]
  32_kHz = female pin header, 1 pin [form="♀ (female)"]
  Batt_+ = female pin header, 1 pin [form="♀ (female)"]
  Batt_- = female pin header, 1 pin [form="♀ (female)"]
  J10 = female pin header, 4 pins [form="♀ (female)"]
  J12 = female pin header, 4 pins [form="♀ (female)"]
  J14 = female pin header, 4 pins [form="♀ (female)"]
  J15 = female pin header, 2 pins [form="♀ (female)"]
  J9 = female pin header, 3 pins [form="♀ (female)"]
  J13 = female pin header, 3 pins [form="♀ (female)"]  # not connected

nets:
  GND: J1.pin1, C6.0, U5.GND, C10.-, C11.0, C12.-, C13.0, U6.GND, J15.pin2
  N1: J1.pin2, U5.D5_(PWM)
  N2: IC3.pin1, U5.D2, J10.pin1, J9.pin1
  N3: IC3.pin2, J7.pin6
  N4: IC3.pin4, IC4.0V, Batt_-.pin1, J12.pin2, J14.pin2
  N5: IC3.pin6, J8.pin4
  N6: IC3.pin7, J8.pin1
  N7: IC3.pin11, J8.pin5
  N8: IC3.pin12, U5.D4, J10.pin3, J9.pin3
  N9: IC3.pin13, U5.D3_(PWM), J10.pin2, J9.pin2
  N10: IC3.pin14, J8.pin2
  N11: IC3.pin15, J8.pin3
  N12: IC3.pin16, J8.pin6
  N13: IC3.pin17, J7.pin5
  N14: IC3.pin18, R7.Pin_1
  N15: IC3.pin19, R7.Pin_0, C6.1, U5.VCC, U5.AVCC, U5.AREF, C10.+, U6.output_voltage, IC4.+V, J10.pin4
  N16: IC3.pin20, J7.pin4
  N17: IC3.pin21, J7.pin1
  N18: IC3.pin22, J7.pin3
  N19: IC3.pin23, J7.pin2
  N20: U5.XLAT1, XTAL3.pin_0, C13.1
  N21: U5.XLAT2, XTAL3.pin_1, C11.1
  N22: U5.A4, IC4.SDA_-_I2C_Data, J12.pin4, J14.pin4
  N23: U5.A5, IC4.SCL_-_I2C_Clock, J12.pin3, J14.pin3
  N24: C12.+, U6.input_voltage, J15.pin1
  N25: IC4.X1_-_Crystal, 32_kHz.pin1
  N26: IC4.X2_-_Crystal, Xtal.pin1
  N27: IC4.Vbat_-_Backup_Supply, Batt_+.pin1
  N28: J12.pin1, J14.pin1
